# Fritzing sketch snake (saved by Fritzing 0.9.3b)
circuit board: 8.46667cm x 5.64444cm
breadboards: 1

parts:
  Part1 = Arduino Nano (Rev3.0)
  R3 = Resistor [tolerance=±5% resistance=1k package=THT]
  R5 = Resistor [tolerance=±5% resistance=1k package=THT]
  R8 = Resistor [tolerance=±5% resistance=2k package=THT]
  R2 = Resistor [tolerance=±5% resistance=1k package=THT]
  R11 = Resistor [tolerance=±5% resistance=2k package=THT]
  R12 = Resistor [tolerance=±5% resistance=2k package=THT]
  R10 = Resistor [tolerance=±5% resistance=2k package=THT]
  Part2 = TFT 2.2 inch 320x240 w microSD [part_number=1480]
  R7 = Resistor [tolerance=±5% resistance=2k package=THT]
  R1 = Resistor [tolerance=±5% resistance=1k package=THT]
  R16 = Resistor [tolerance=±5% resistance=2k package=THT]
  R6 = Resistor [tolerance=±5% resistance=1k package=THT]
  R14 = Resistor [tolerance=±5% resistance=2k package=THT]
  R15 = Resistor [tolerance=±5% resistance=2k package=THT]
  R13 = Resistor [tolerance=±5% resistance=2k package=THT]
  R9 = Resistor [tolerance=±5% resistance=2k package=THT]
  R4 = Resistor [tolerance=±5% resistance=1k package=THT]
  S4 = Pushbutton [package="[SMD]"]
  S2 = Pushbutton [package="[SMD]"]
  S3 = Pushbutton [package="[SMD]"]
  S1 = Pushbutton [package="[SMD]"]

nets:
  GND: Part1.GND, R3.Pin_0, R5.Pin_0, R2.Pin_0, Part2.GND, Part2.SDCS, R1.Pin_0, R16.Pin_1, R6.Pin_0, R14.Pin_1, R15.Pin_1, R13.Pin_1, R4.Pin_0
  N1: Part1.D2, R16.Pin_0, S1.Pin_3, S1.Pin_4
  N2: Part1.D3, R15.Pin_0, S2.Pin_3, S2.Pin_4
  N3: Part1.D4, R14.Pin_0, S3.Pin_3, S3.Pin_4
  N4: Part1.D5, R13.Pin_0, S4.Pin_3, S4.Pin_4
  N5: Part1.D8, R12.Pin_1
  N6: Part1.D9, R11.Pin_1
  N7: Part1.D10, R10.Pin_1
  N8: Part1.D11/MOSI, R9.Pin_1
  N9: Part1.D12/MISO, R8.Pin_1
  N10: Part1.5V, S4.Pin_1, S4.Pin_2, S2.Pin_1, S2.Pin_2, S3.Pin_1, S3.Pin_2, S1.Pin_1, S1.Pin_2
  3V3: Part1.3V3, Part2.VIN, Part2.BACKLIGHT
  N11: Part1.D13/SCK, R7.Pin_1
  N12: R3.Pin_1, Part2.MOSI, R9.Pin_0
  N13: R5.Pin_1, R11.Pin_0, Part2.DC
  N14: R8.Pin_0, R2.Pin_1, Part2.MISO
  N15: R12.Pin_0, Part2.RESET, R6.Pin_1
  N16: R10.Pin_0, Part2.LCDCS, R4.Pin_1
  N17: Part2.SCLK, R7.Pin_0, R1.Pin_1

notes:
  If your screen has SDcard, make sure to disable it
  Disable screen SDCard

custom parts:
  TFT 2.2 inch 320x240 w microSD: This lovely little display breakout is the best way to add a small, colorful and bright display to any project. Since the display uses 4-wire SPI to communicate and has its own pixel-addressable frame buffer, it can be used with every kind of microcontroller. Even a very small one with low memory and few pins available! The 2.2" display has 320x240 color pixels.
